# Fritzing sketch gpioLab (saved by Fritzing 0.7.5b)
breadboards: 1

parts:
  BeagleBone1 = beaglebone-a5
  LED1 = LED - 5mm [color="Red (633nm)" package="5 mm [THT]"]
  R1 = Resistor [tolerance=±5% resistance=220 package=THT]
  S1 = Pushbutton [package="[THT]"]
  R2 = Resistor [tolerance=±5% resistance=220 package=THT]
  R3 = Trimmer Potentiometer [maximum_resistance=10kΩ package=THT]
  Part1 = Digital Temperature Sensor Breakout - TMP102
  R4 = Resistor [tolerance=±5% resistance=4.7k package=THT]
  R5 = Resistor [tolerance=±5% resistance=4.7k package=THT]

nets:
  N1: BeagleBone1.connectorp9-1, R1.Pin_1, Part1.GND
  N2: BeagleBone1.connectorp9-3, R2.Pin_1, Part1.V+, R4.Pin_1, R5.Pin_1
  N3: BeagleBone1.connectorp9-12, LED1.cathode
  N4: BeagleBone1.connectorp9-19, Part1.SCL, R5.Pin_0
  N5: BeagleBone1.connectorp9-20, Part1.SDA, R4.Pin_0
  N6: BeagleBone1.connectorp9-32, R3.leg1
  N7: BeagleBone1.connectorp9-34, R3.leg2
  N8: BeagleBone1.connectorp9-36, R3.wiper
  N9: BeagleBone1.connectorp9-42, S1.Pin_1, S1.Pin_2, S1.Pin_3, S1.Pin_4, R2.Pin_0
  N10: LED1.anode, R1.Pin_0
