# Fritzing sketch wiring (saved by Fritzing 0.8.5b)
breadboards: 1

parts:
  BeagleBone1 = BeagleBone Black
  LPD8806_RGB_LED_Strip1 = LPD8806 RGB LED Strip

nets:
  N1: BeagleBone1.no_name_yet#1, LPD8806_RGB_LED_Strip1.GND
  N2: BeagleBone1.no_name_yet#3, LPD8806_RGB_LED_Strip1.+5V
  N3: BeagleBone1.no_name_yet#30, LPD8806_RGB_LED_Strip1.CI
  N4: BeagleBone1.no_name_yet#31, LPD8806_RGB_LED_Strip1.DI

notes:
  +
  -
  P9
  P8

custom parts:
  BeagleBone Black: BeagleBone Black rev. A5B
  LPD8806 RGB LED Strip: Digitally addressable RGB LED strip
