# Fritzing sketch Lab02 (saved by Fritzing 0.8.5b)
breadboards: 1

parts:
  BeagleBone1 = BeagleBone Black
  LED1 = LED - 5mm [color="Red (633nm)" package="5 mm [THT]"]
  R1 = Resistor [tolerance=±5% resistance=220 package=THT]
  S2 = Pushbutton [package="[THT]"]
  S3 = Pushbutton [package="[THT]"]
  R2 = Resistor [tolerance=±5% resistance=220 package=THT]
  LED2 = LED - 5mm [color="Red (633nm)" package="5 mm [THT]"]

nets:
  N1: BeagleBone1.no_name_yet#1, R1.Pin_1, R2.Pin_1
  N2: BeagleBone1.no_name_yet#3, S2.Pin_3, S2.Pin_4, S3.Pin_3, S3.Pin_4
  N3: BeagleBone1.no_name_yet#12, LED1.anode
  N4: BeagleBone1.no_name_yet#20, LED2.anode
  N5: BeagleBone1.no_name_yet#26, S3.Pin_1, S3.Pin_2
  N6: BeagleBone1.no_name_yet#42, S2.Pin_1, S2.Pin_2
  N7: LED1.cathode, R1.Pin_0
  N8: R2.Pin_0, LED2.cathode

custom parts:
  BeagleBone Black: BeagleBone Black rev. A5B
