# Fritzing sketch Lab03 (saved by Fritzing 0.8.5b)
breadboards: 1

parts:
  BeagleBone1 = BeagleBone Black
  LED1 = LED - 5mm [color="Red (633nm)" package="5 mm [THT]"]
  R1 = Resistor [tolerance=±5% resistance=220 package=THT]
  S2 = Pushbutton [package="[THT]"]
  R2 = Resistor [tolerance=±5% resistance=220 package=THT]
  LED2 = LED - 5mm [color="Red (633nm)" package="5 mm [THT]"]
  R3 = Trimmer Potentiometer [maximum_resistance=10kΩ package=THT]

nets:
  N1: BeagleBone1.no_name_yet#1, R1.Pin_1, R2.Pin_1
  N2: BeagleBone1.no_name_yet#3, S2.Pin_3, S2.Pin_4
  N3: BeagleBone1.no_name_yet#14, LED1.anode
  N4: BeagleBone1.no_name_yet#16, LED2.anode
  N5: BeagleBone1.no_name_yet#32, R3.leg2
  N6: BeagleBone1.no_name_yet#34, R3.leg1
  N7: BeagleBone1.no_name_yet#36, R3.wiper
  N8: BeagleBone1.no_name_yet#42, S2.Pin_1, S2.Pin_2
  N9: LED1.cathode, R1.Pin_0
  N10: R2.Pin_0, LED2.cathode

custom parts:
  BeagleBone Black: BeagleBone Black rev. A5B
