# Fritzing sketch motionSensor (saved by Fritzing 0.9.3b)
breadboards: 1

parts:
  BeagleBone1 = BeagleBone Black
  PIR1 = PIR sensor
  R1 = Resistor [tolerance=±5% resistance=10k package="2010 [SMD]"]
  R2 = Resistor [tolerance=±5% resistance=10k package="2010 [SMD]"]
  LED1 = smd LED [color="Red (633nm)" package="1206 [SMD]"]
  R3 = Resistor [tolerance=±5% resistance=470 package="2010 [SMD]"]

nets:
  N1: BeagleBone1.no_name_yet#1, PIR1.GND, LED1.cathode
  N2: BeagleBone1.no_name_yet#5, R1.Pin_1
  N3: BeagleBone1.no_name_yet#14, R3.Pin_1
  N4: BeagleBone1.no_name_yet#118, R2.Pin_0
  N5: PIR1.VDD, R1.Pin_0
  N6: PIR1.SIG, R2.Pin_1
  N7: LED1.anode, R3.Pin_0

notes:
  +
  -
  P9
  P8

custom parts:
  BeagleBone Black: BeagleBone Black rev. A5B
