# Fritzing sketch bmp085 (saved by Fritzing 0.8.5b)
breadboards: 1

parts:
  BeagleBone1 = BeagleBone Black
  Part1 = Barometric Pressure Sensor - BMP085 Breakout
  R1 = Resistor [tolerance=±5% resistance=1k package=THT]
  R2 = Resistor [tolerance=±5% resistance=1k package=THT]

nets:
  N1: BeagleBone1.no_name_yet#1, BeagleBone1.no_name_yet#41, Part1.GND, R1.Pin_0, R2.Pin_1
  N2: BeagleBone1.no_name_yet#3, Part1.VCC
  N3: BeagleBone1.no_name_yet#19, Part1.SDA
  N4: BeagleBone1.no_name_yet#20, Part1.SCL
  N5: BeagleBone1.no_name_yet#42, R1.Pin_1, R2.Pin_0

notes:
  +
  -
  P9
  P8
  Power Soil Moisture Sensor from P9_41 so we can turn it on when needed.
  Run SIG through a voltage divider to keep output below 1.8V.

custom parts:
  BeagleBone Black: BeagleBone Black rev. A5B
