# Fritzing sketch launchPad (saved by Fritzing 0.8.7b)

parts:
  BeagleBone1 = BeagleBone Black
  Launchpad1 = TI Launchpad MSP430G2

nets:
  N1: BeagleBone1.no_name_yet#1, Launchpad1.p20
  N2: BeagleBone1.no_name_yet#24, Launchpad1.p3
  N3: BeagleBone1.no_name_yet#26, Launchpad1.p4

notes:
  +
  -
  P9
  P8

custom parts:
  BeagleBone Black: BeagleBone Black rev. A5B
