# Fritzing sketch bmp085 (saved by Fritzing 0.8.5b)
breadboards: 1

parts:
  BeagleBone1 = BeagleBone Black
  Part1 = Barometric Pressure Sensor - BMP085 Breakout

nets:
  N1: BeagleBone1.no_name_yet#1, Part1.GND
  N2: BeagleBone1.no_name_yet#3, Part1.VCC
  N3: BeagleBone1.no_name_yet#19, Part1.SDA
  N4: BeagleBone1.no_name_yet#20, Part1.SCL

notes:
  +
  -
  P9
  P8

custom parts:
  BeagleBone Black: BeagleBone Black rev. A5B
