# Fritzing sketch ti-rslk (saved by Fritzing 0.9.3b)

parts:
  JP1 = M10X2 [package=2x10_lock]
  Part1 = PocketBeagle
  JP2 = M10X2 [package=2x10_lock]
  JP3 = M10X2 [package=2x10_lock]  # not connected
  JP4 = M10X2 [package=2x10_lock]

nets:
  N1: JP1.1, Part1.PWM1A
  N2: JP1.3, Part1.PWM0A
  N3: JP1.15, Part1.GPIO45
  N4: JP1.17, Part1.PRU0.5
  N5: Part1.GND, JP2.4
  N6: Part1.PRU0.4, JP4.14
  N7: Part1.GPIO26, JP2.20
  N8: Part1.GPIO60, JP2.18
  N9: Part1.BAT.VIN, JP4.13
