# Fritzing sketch onewire (saved by Fritzing 0.8.7b)
breadboards: 1

parts:
  BeagleBone1 = BeagleBone Black
  DS1 = DS18B20 1-Wire Temperature Sensor [part_number=DS18B20]
  R1 = Resistor [tolerance=±5% resistance=4.7k package=THT]

nets:
  N1: BeagleBone1.no_name_yet#1, DS1.GND
  N2: BeagleBone1.no_name_yet#3, DS1.VDD, R1.Pin_1
  N3: BeagleBone1.no_name_yet#12, DS1.DQ, R1.Pin_0

custom parts:
  BeagleBone Black: BeagleBone Black rev. A5B
